# Fritzing sketch arduino (saved by Fritzing 0.9.3b)
circuit board: 8.46667cm x 5.64444cm
breadboards: 1

parts:
  Part1 = Arduino Mega 2560 (Rev3)
  fl1 = Rotary Potentiometer (Large) [maximum_resistance=100kΩ package=THT]
  fl2 = Rotary Potentiometer (Large) [maximum_resistance=100kΩ package=THT]
  bp1 = Rotary Potentiometer (Large) [maximum_resistance=100kΩ package=THT]
  R1 = Resistor [tolerance=±5% resistance=220 package=THT]
  R2 = Resistor [tolerance=±5% resistance=220 package=THT]
  R3 = Resistor [tolerance=±5% resistance=220 package=THT]
  R4 = Resistor [tolerance=±5% resistance=220 package=THT]
  R5 = Resistor [tolerance=±5% resistance=220 package=THT]
  J1 = Camdenboss CTB0158-12 [part_number=CTB0158-12 package=THT]
  ot1 = Rotary Potentiometer (Large) [maximum_resistance=100kΩ package=THT]
  wt1 = Rotary Potentiometer (Large) [maximum_resistance=100kΩ package=THT]
  op1 = Rotary Potentiometer (Large) [maximum_resistance=100kΩ package=THT]
  R6 = Resistor [tolerance=±5% resistance=220 package=THT]
  rs1 = Hall Sensor [package="TO92 [THT]"]
  es2 = Hall Sensor [package="TO92 [THT]"]
  J2 = Camdenboss CTB0158-6 [part_number=CTB0158-6 package=THT]
  J5 = Camdenboss CTB0158-12 [part_number=CTB0158-12 package=THT]
  R7 = Resistor [tolerance=±5% resistance=6.8k package=THT]
  R8 = Resistor [tolerance=±5% resistance=100k package=THT]
  J6 = Camdenboss CTB0158-2 [part_number=CTB0158-2 package=THT]
  S1 = Momentary Switch [package=tactile-pth]
  U1 = MCP42xxx [package=so014]
  J7 = Camdenboss CTB0158-6 [part_number=CTB0158-6 package=THT]
  dl1 = NPN-Transistor [package="TO92 [THT]"]
  dl2 = NPN-Transistor [package="TO92 [THT]"]
  J8 = Camdenboss CTB0158-6 [part_number=CTB0158-6 package=THT]
  R9 = Resistor [tolerance=±5% resistance=2.2k package=THT]
  R10 = Resistor [tolerance=±5% resistance=2.2k package=THT]
  U3 = OPTO_DARL_6N138S [package=8-smd]
  U4 = OPTO_DARL_6N138S [package=8-smd]
  R11 = Resistor [tolerance=±5% resistance=220 package=THT]
  R12 = Resistor [tolerance=±5% resistance=220 package=THT]
  J9 = Camdenboss CTB0158-4 [part_number=CTB0158-4 package=THT]
  opl1 = SWITCH-MOMENTARY-2 [package=reed_switch_pth]
  bpl1 = SWITCH-MOMENTARY-2 [package=reed_switch_pth]
  Part2 = DeuLigne 1.1 - The Snootlab's LCD shield for Arduino

nets:
  N1: Part1.A9, R7.Pin_1, R8.Pin_0
  N2: Part1.A10, J5.pin5
  N3: Part1.A11, J5.pin2
  N4: Part1.A12, J1.pin8
  N5: Part1.A13, J1.pin5
  N6: Part1.A14, J1.pin2
  N7: Part1.A15, J5.pin8
  N8: Part1.D21/SCL, Part1.SCL, U1.SCK
  N9: Part1.D19/RX1, Part2.D1_TX
  N10: Part1.D18/TX1, Part2.D0_RX
  N11: Part1.SDA, U1.DI
  N12: Part1.RESET, S1.3
  N13: Part1.D2_PWM, J2.pin2
  N14: Part1.D3_PWM, J2.pin5
  N15: Part1.5V, R1.Pin_0, R2.Pin_0, R3.Pin_0, R4.Pin_0, R5.Pin_0, R6.Pin_0
  N16: Part1.D22, R10.Pin_1
  N17: Part1.D23, R9.Pin_1
  N18: Part1.D24, U3.VOUT
  N19: Part1.D25, U4.VOUT
  N20: fl1.leg1, J1.terminal_7
  N21: fl1.wiper, J1.terminal_8
  N22: fl1.leg2, J1.terminal_9
  N23: fl2.leg1, J5.terminal_1
  N24: fl2.wiper, J5.terminal_2
  N25: fl2.leg2, J5.terminal_3
  N26: bp1.leg1, J5.terminal_4
  N27: bp1.wiper, J5.terminal_5
  N28: bp1.leg2, J5.terminal_6
  N29: R1.Pin_1, J1.pin1
  N30: R2.Pin_1, J1.pin4
  N31: R3.Pin_1, J1.pin7
  N32: R4.Pin_1, J5.pin1
  N33: R5.Pin_1, J5.pin4
  GND: J1.pin3, J1.pin6, J1.pin9, J1.pin12, J2.pin3, J2.pin6, J5.pin3, J5.pin6, J5.pin9, J5.pin12, R7.Pin_0, S1.1, U1.GND, dl1.E, dl2.E, U3.GND, U4.GND, opl1.1, bpl1.1, Part2.GND
  N34: J1.terminal_1, ot1.leg1
  N35: J1.terminal_2, ot1.wiper
  N36: J1.terminal_3, ot1.leg2
  N37: J1.terminal_4, wt1.leg1
  N38: J1.terminal_5, wt1.wiper
  N39: J1.terminal_6, wt1.leg2
  N40: op1.leg1, J5.terminal_7
  N41: op1.wiper, J5.terminal_8
  N42: op1.leg2, J5.terminal_9
  N43: R6.Pin_1, J5.pin7
  N44: rs1.+Vs, J2.terminal_1
  N45: rs1.Vout, J2.terminal_2
  N46: rs1.GND, J2.terminal_3
  N47: es2.+Vs, J2.terminal_4
  N48: es2.Vout, J2.terminal_5
  N49: es2.GND, J2.terminal_6
  VCC: J2.pin1, J2.pin4, U1.VCC, Part2.+5V
  N50: R8.Pin_1, J6.pin1
  N51: U1.B1, J7.pin6
  N52: U1.W1, J7.pin5
  N53: U1.A1, J7.pin4
  N54: U1.A0, J7.pin1
  N55: U1.W0, J7.pin2
  N56: U1.B0, J7.pin3
  N57: dl1.B, R10.Pin_0
  N58: dl1.C, J8.pin2
  N59: dl2.B, R9.Pin_0
  N60: dl2.C, J8.pin4
  N61: U3.A, R11.Pin_0
  N62: U3.C, J9.pin2
  VCC_2: U3.VCC, U4.VCC
  N63: U4.A, R12.Pin_0
  N64: U4.C, J9.pin4
  N65: R11.Pin_1, J9.pin1
  N66: R12.Pin_1, J9.pin3
  12V: J9.terminal_1, J9.terminal_3
  N67: J9.terminal_2, opl1.2
  N68: J9.terminal_4, bpl1.2

// code stored in the sketch: arduino_schem.ino


//////////////////////////////////////////////////////
/*
  0 - ~16volt voltmeter for 3.3volt and 5volt Arduinos
  uses the stable internal 1.1volt reference
  6k8 resistor from A0 to ground, and 100k resistor from A0 to +batt
  100n capacitor from A0 to ground for stable readings
  (100k + 6k8) / 6k8 = 15.70588 | used in formula
*/
float Aref = 1.075; // ***calibrate here*** | change this to the actual Aref voltage of ---YOUR--- Arduino
unsigned int total; // can hold max 64 readings
float voltage; // converted to volt

void setup() {
  analogReference(INTERNAL); // use the internal ~1.1volt reference  | change (INTERNAL) to (INTERNAL1V1) for a Mega
  Serial.begin(9600); // set serial monitor to this value
}

void loop() {
  for (int x = 0; x < 64; x++) { // multiple analogue readings for averaging
    total = total + analogRead(A0); // add each value to a total
  }
  voltage = (total / 64) * 15.70588 * Aref / 1024 ; // convert readings to volt
  // print to serial monitor
  if (total == (1023 * 64)) { // if overflow
    Serial.print("voltage too high");
  }
  else {
    Serial.print("The battery is ");
    Serial.print(voltage);
    Serial.println(" volt");
  }
  total = 0; // reset value
  delay(1000); // one second between measurements
}

//////////////////////////////////////////////////////////////
